# Fritzing sketch esquema_elétrico (saved by Fritzing 0.9.2b)
breadboards: 1

parts:
  U1 = NodeMCU V1.0
  J1 = Piezo Speaker
  R1 = Resistor [tolerance=±5% resistance=10k package=THT]
  R2 = Resistor [tolerance=±5% resistance=10k package=THT]
  R3 = Resistor [tolerance=±5% resistance=10k package=THT]
  Q1 = npn-Powertransistor [part_number=TIP122 package="TO220 [THT]"]
  Q2 = npn-Powertransistor [part_number=TIP122 package="TO220 [THT]"]
  Q3 = npn-Powertransistor [part_number=TIP122 package="TO220 [THT]"]
  LED1 = LED - 5mm [color="Red (633nm)" package="5 mm [THT]"]
  LED2 = LED - 5mm [color="Yellow (585nm)" package="5 mm [THT]"]
  R4 = Resistor [tolerance=±5% resistance=330 package=THT]
  R5 = Resistor [tolerance=±5% resistance=330 package=THT]
  VCC1 = 4 x AAA Battery Mount

nets:
  N1: U1.D0, R2.Pin_0
  N2: U1.D1, R1.Pin_0
  N3: U1.D2, R3.Pin_0
  N4: U1.GND, Q1.collector, Q2.collector, Q3.collector, VCC1.-
  N5: U1.Vin, J1.pin2, R4.Pin_0, R5.Pin_0, VCC1.+
  N6: J1.pin1, Q1.emitter
  N7: R1.Pin_1, Q2.base
  N8: R2.Pin_1, Q1.base
  N9: R3.Pin_1, Q3.base
  N10: Q2.emitter, LED1.cathode
  N11: Q3.emitter, LED2.cathode
  N12: LED1.anode, R4.Pin_1
  N13: LED2.anode, R5.Pin_1

custom parts:
  NodeMCU V1.0: ESP9266 based NodeMCU
